# Fritzing sketch modulo mcu (saved by Fritzing 1.0.2b)
circuit board: 11.2cm x 8.2cm
breadboards: 1

parts:
  4CH_Logical_Level_Adapter = Logic Level Converter
  Buck_Converter_(5V) = LM2596 step down module
  Arduino_Nano_v3 = Arduino Nano (Rev3.0)
  E32-868T30D = ossoyoo-lora-module
  GND_+12V = Screw terminal - 2 pins [package=THT]
  J5 = Dagu DGServo 9g header (male) [package=THT]
  J6 = Dagu DGServo 9g header (male) [package=THT]
  C1 = Electrolytic Capacitor [capacitance=1µF package="100 mil [THT, electrolytic]"]
  R1 = Resistor [tolerance=±5% resistance=220 power=0.25W package=THT]
  LED1 = LED - 5mm [color="Red (633nm)" current=0.030A package="5 mm [THT]"]

nets:
  GND: 4CH_Logical_Level_Adapter.GND, Buck_Converter_(5V).IN-, Buck_Converter_(5V).OUT-, Arduino_Nano_v3.GND, E32-868T30D.M1, E32-868T30D.GND, GND_+12V.pin2, J6.gnd, C1.-, LED1.cathode
  N1: 4CH_Logical_Level_Adapter.LV, Arduino_Nano_v3.3V3, E32-868T30D.M0
  N2: 4CH_Logical_Level_Adapter.RX_LV, E32-868T30D.TXD
  N3: 4CH_Logical_Level_Adapter.TX_LV, E32-868T30D.RXD
  N4: 4CH_Logical_Level_Adapter.TX_HV, Arduino_Nano_v3.D9
  N5: 4CH_Logical_Level_Adapter.RX_HV, Arduino_Nano_v3.D10
  5V: 4CH_Logical_Level_Adapter.HV, Buck_Converter_(5V).OUT+, Arduino_Nano_v3.5V, E32-868T30D.VCC, J6.pulse
  N6: Buck_Converter_(5V).IN+, GND_+12V.pin1, J6.Vcc
  N7: Arduino_Nano_v3.RESET, J5.Vcc, C1.+
  N8: Arduino_Nano_v3.A5, J5.gnd
  N9: Arduino_Nano_v3.A4, J5.pulse
  N10: Arduino_Nano_v3.D13/SCK, R1.Pin_0
  N11: R1.Pin_1, LED1.anode

notes:
  SDA
  RST
  SCL
  GND
  5V
  12V

custom parts:
  LM2596 step down module: LM2596 DC-DC step down power supply module 3 A.
  ossoyoo-lora-module: Osoyoo Long Distance wireless transceiver Uart LoRa Module.
