# Fritzing sketch ricevitore (saved by Fritzing 1.0.2b)
circuit board: 8.2cm x 6.5cm

parts:
  E32-868T20D = ossoyoo-lora-module
  C2 = Electrolytic Capacitor [capacitance=2.2µF voltage=6.3V package="100 mil [THT, electrolytic]"]
  TB6612FNG = Motor Driver 1A Dual TB6612FNG
  TB6612FNG_2 = Motor Driver 1A Dual TB6612FNG
  Arduino_Pro_Mini_3_3V = Arduino Pro Mini v13
  MCP1702-33 = MCP1702 Voltage Regulator [package="TO92 [THT]"]
  C1 = Electrolytic Capacitor [capacitance=2.2µF voltage=6.3V package="100 mil [THT, electrolytic]"]
  VCC_GND = screw terminal, 2 pins
  V1+_V1- = screw terminal, 2 pins
  V2-_V2+ = screw terminal, 2 pins
  V3+_V3- = screw terminal, 2 pins
  V4-_V4+ = screw terminal, 2 pins

nets:
  GND: E32-868T20D.M0, E32-868T20D.GND, C2.-, TB6612FNG.GND, TB6612FNG_2.GND, Arduino_Pro_Mini_3_3V.GND, MCP1702-33.GND, C1.-, VCC_GND.pin1
  VCC: E32-868T20D.M1, E32-868T20D.VCC, C2.+, TB6612FNG.VCC, TB6612FNG_2.VCC, Arduino_Pro_Mini_3_3V.VCC, MCP1702-33.Vout
  N1: E32-868T20D.RXD, Arduino_Pro_Mini_3_3V.D0/TX
  N2: E32-868T20D.TXD, Arduino_Pro_Mini_3_3V.D1/RX
  N3: E32-868T20D.AUX, Arduino_Pro_Mini_3_3V.D2
  N4: TB6612FNG.B01, V2-_V2+.pin1
  N5: TB6612FNG.B02, V2-_V2+.pin2
  N6: TB6612FNG.A02, V1+_V1-.pin1
  N7: TB6612FNG.A01, V1+_V1-.pin2
  N8: TB6612FNG.VM, TB6612FNG_2.VM, MCP1702-33.Vin, C1.+, VCC_GND.pin2
  N9: TB6612FNG.PWMA, TB6612FNG.STBY, TB6612FNG.PWMB, TB6612FNG_2.PWMA, TB6612FNG_2.STBY, TB6612FNG_2.PWMB, Arduino_Pro_Mini_3_3V.D3_PWM
  N10: TB6612FNG.AIN2, Arduino_Pro_Mini_3_3V.D4
  N11: TB6612FNG.AIN1, Arduino_Pro_Mini_3_3V.D5_PWM
  N12: TB6612FNG.BIN1, Arduino_Pro_Mini_3_3V.D6_PWM
  N13: TB6612FNG.BIN2, Arduino_Pro_Mini_3_3V.D7
  N14: TB6612FNG_2.B01, V4-_V4+.pin1
  N15: TB6612FNG_2.B02, V4-_V4+.pin2
  N16: TB6612FNG_2.A02, V3+_V3-.pin1
  N17: TB6612FNG_2.A01, V3+_V3-.pin2
  N18: TB6612FNG_2.AIN2, Arduino_Pro_Mini_3_3V.D8
  N19: TB6612FNG_2.AIN1, Arduino_Pro_Mini_3_3V.D9_PWM
  N20: TB6612FNG_2.BIN1, Arduino_Pro_Mini_3_3V.D11_PWM/MOSI
  N21: TB6612FNG_2.BIN2, Arduino_Pro_Mini_3_3V.D10_PWM/SS

custom parts:
  ossoyoo-lora-module: Osoyoo Long Distance wireless transceiver Uart LoRa Module.
  MCP1702 Voltage Regulator: A MCP1702 Low Dropout Fixed Voltage Regulator (available in 1.2V, 1.5V, 1.8V, 2.5V, 2.8V, 3.0V, 3.3V, 4.0V, 5.0V)
